# Fritzing sketch feeder (saved by Fritzing 0.9.3b)
perfboards: 1

parts:
  J1 = double row smd male pin header, 20 pins [form="♂ (male)"]
  S1 = Pushbutton [package="[THT]"]
  J2 = double row smd male pin header, 20 pins [form="♂ (male)"]
  LED1 = LED - 3mm [color="Red (633nm)" package="3 mm [THT]"]
  J3 = female pin header, 3 pins [form="♀ (female)"]
  J5 = female pin header, 6 pins [form="♀ (female)"]
  J4 = male pin header, 4 pins [form="♂ (male)"]
  R5 = Resistor Mini [tolerance=±5% resistance=220 package=THT]
  R6 = Resistor Mini [tolerance=±5% resistance=220 package=THT]

nets:
  N1: J1.pin12, S1.Pin_1, S1.Pin_2
  N2: J1.pin13, J5.pin2
  N3: J1.pin14, J5.pin3
  N4: J1.pin15, J5.pin4
  N5: J1.pin18, J4.pin2
  N6: J1.pin19, J4.pin3
  N7: S1.Pin_3, S1.Pin_4, J2.pin1
  N8: J2.pin4, R5.Pin_1, R6.Pin_0
  N9: J2.pin9, LED1.anode
  N10: J2.pin15, J5.pin5
  N11: J2.pin17, J3.pin2
  N12: J2.pin20, J4.pin4
  N13: LED1.cathode, R6.Pin_1
  N14: J3.pin1, J5.pin6
  N15: J5.pin1, J4.pin1

notes:
  3V3
  Step Motor
  LCD Panel
  5V0
  DHT11

custom parts:
  Resistor Mini: A generic resistor (0.25W)
